# Fritzing sketch electrocute (saved by Fritzing 0.7.12b)
breadboards: 1

parts:
  Arduino1 = Arduino
  LED1 = LED - 5mm [color="Red (633nm)" package="5 mm [THT]"]
  R1 = Resistor [tolerance=±5% resistance=1k package=THT]
  LED2 = LED - 5mm [color="Red (633nm)" package="5 mm [THT]"]
  R2 = Resistor [tolerance=±5% resistance=1k package=THT]
  R3 = Resistor [tolerance=±5% resistance=1k package=THT]
  LED3 = LED - 5mm [color="Red (633nm)" package="5 mm [THT]"]
  R4 = Resistor [tolerance=±5% resistance=470k package=THT]
  R5 = Resistor [tolerance=±5% resistance=470k package=THT]
  R6 = Resistor [tolerance=±5% resistance=470k package=THT]

nets:
  N1: Arduino1.D11, R3.Pin_0
  N2: Arduino1.D10, R2.Pin_0
  N3: Arduino1.D9, R1.Pin_0
  N4: Arduino1.GND, LED1.anode, LED2.anode, LED3.anode, R4.Pin_0, R5.Pin_0, R6.Pin_0
  N5: Arduino1.A0, R6.Pin_1
  N6: Arduino1.A1, R5.Pin_1
  N7: Arduino1.A2, R4.Pin_1
  N8: LED1.cathode, R1.Pin_1
  N9: LED2.cathode, R2.Pin_1
  N10: R3.Pin_1, LED3.cathode

notes:
  ELECTROCUTE, Circuit diagram - ecpobox.blogspot.com, 1
  ecpobox.blogspot.com
  electrocute
  by deadman
